# Fritzing sketch sumobot (saved by Fritzing 1.0.6)

parts:
  L298N_(Pont_H) = H-Bridge with L298N
  Moteur_Gauche = DC Motor [voltage_(max)=6V voltage_(min)=3V]
  Moteur_Droit = DC Motor [voltage_(max)=6V voltage_(min)=3V]
  Bouton_START = Pushbutton [package="[THT]"]
  LM2596_Buck = mystery part, 3 pins [chip_label=LM2596 pins=3]
  Arduino_Mega_2560 = Arduino Mega 2560 (Rev3)

nets:
  N1: L298N_(Pont_H).ENA, Arduino_Mega_2560.D10_PWM
  N2: L298N_(Pont_H).IN1, Arduino_Mega_2560.D9_PWM
  N3: L298N_(Pont_H).IN2, Arduino_Mega_2560.D8_PWM
  N4: L298N_(Pont_H).IN3, Arduino_Mega_2560.D6_PWM
  N5: L298N_(Pont_H).IN4, Arduino_Mega_2560.D7_PWM
  N6: L298N_(Pont_H).ENB, Arduino_Mega_2560.D5_PWM
  N7: L298N_(Pont_H).M1-01, Moteur_Gauche.pin_2
  N8: L298N_(Pont_H).M1-02, Moteur_Gauche.pin_1
  N9: L298N_(Pont_H).M2-01, Moteur_Droit.pin_2
  N10: L298N_(Pont_H).M2-02, Moteur_Droit.pin_1
  N11: Bouton_START.Pin_1, Bouton_START.Pin_2, Arduino_Mega_2560.GND, Arduino_Mega_2560.D2_PWM
  N12: LM2596_Buck.pin2, Arduino_Mega_2560.5V

notes:
  SUMOBOT — Schema de cablage. Ajouter manuellement: VL53L0X x3, TCRT5000 x3, MPU6050 (importer les .fzpz).
  CAPTEURS A AJOUTER:
  - 3x VL53L0X: SDA→Pin20, SCL→Pin21, XSHUT→Pin22/23/24
  - 3x TCRT5000: Signal→A0/A1/A2, VCC→5V, GND
  - 1x MPU6050: SDA→Pin20, SCL→Pin21, AD0→GND
  LM2596 Buck: pin1=Vin(7.5V), pin2=Vout(5V), pin3=GND

custom parts:
  H-Bridge with L298N: h-bridge
